// Logisim project Final.circ as structural Verilog: 2 circuits, main circuit main
module main (
  output [3:0] OutFlag,
  output [7:0] out_2,
  output [7:0] out_3
);

  wire clk, enable, l_h, muxC, read;
  wire [1:0] funsel_AR, funsel_IR, funsel_R, muxA, muxB, outA_R, outB_R, outC_AR, outD_AR;
  wire [2:0] regsel_AR;
  wire [3:0] ALU_zcno, funsel_ALU, main_1_outa, main_1_outa_2, multiplexer_3_out, multiplexer_3_out_2,
       ram_1_data, ram_1_data_2, regsel_R;
  wire [7:0] Adress_Register_File_outc, Adress_Register_File_outd, ALU_outalu, main_1_outb,
       multiplexer_1_out, multiplexer_2_out;

  controller controller_1 (
    .clock(clk), .Z_Flag(OutFlag[3]), .instruction({out_3, out_2}), .enable(enable), .l_h(l_h),
    .\funsel_ır (funsel_IR), .read(read), .regsel_ar(regsel_AR), .funsel_ar(funsel_AR), .outd_ar(outD_AR));  // open: out_4
  Hex_Digit_Display hex_digit_display_1 (.value(multiplexer_2_out[7:4]));  // open: dp
  Hex_Digit_Display hex_digit_display_2 (.value(multiplexer_2_out[3:0]));  // open: dp
  Hex_Digit_Display hex_digit_display_3 (.value(main_1_outa_2));  // open: dp
  Hex_Digit_Display hex_digit_display_4 (.value(main_1_outa));  // open: dp
  Hex_Digit_Display hex_digit_display_5 (.value(out_2[7:4]));  // open: dp
  Hex_Digit_Display hex_digit_display_6 (.value(out_2[3:0]));  // open: dp
  _8_bit_register_file_2a__main main_1 (
    .FunSel(funsel_R), .Input(multiplexer_2_out), .OutA({main_1_outa_2, main_1_outa}), .OutB(main_1_outb),
    .OutBSel(outB_R), .OutASel(outA_R), .RegSel(regsel_R), .Clock(clk));
  Hex_Digit_Display hex_digit_display_7 (.value(ram_1_data_2));  // open: dp
  Hex_Digit_Display hex_digit_display_8 (.value(main_1_outb[7:4]));  // open: dp
  Hex_Digit_Display hex_digit_display_9 (.value(main_1_outb[3:0]));  // open: dp
  Multiplexer #(.width(8), .enable("false")) multiplexer_1 (
    .in0(Adress_Register_File_outc), .in1({main_1_outa_2, main_1_outa}), .out(multiplexer_1_out), .sel(muxC));
  Multiplexer #(.select(2), .width(8), .enable("false")) multiplexer_2 (
    .in0(out_2), .in1({ram_1_data_2, ram_1_data}), .in2(Adress_Register_File_outc), .in3(ALU_outalu),
    .out(multiplexer_2_out), .sel(muxA));
  Hex_Digit_Display hex_digit_display_10 (.value(ram_1_data));  // open: dp
  _2_c_main _16_Bit_Register (
    .in_3({ram_1_data_2, ram_1_data}), .out_7({out_3, out_2}), .low_high(l_h), .in_5(funsel_IR[1]),
    .in_6(funsel_IR[0]), .enable(enable), .clock(clk));
  Hex_Digit_Display hex_digit_display_11 (.value(out_3[7:4]));  // open: dp
  Hex_Digit_Display hex_digit_display_12 (.value(out_3[3:0]));  // open: dp
  Hex_Digit_Display hex_digit_display_13 (.value(multiplexer_1_out[7:4]));  // open: dp
  Hex_Digit_Display hex_digit_display_14 (.value(multiplexer_3_out_2));  // open: dp
  Multiplexer #(.select(2), .width(8), .enable("false")) multiplexer_3 (
    .in1(out_2), .in2({ram_1_data_2, ram_1_data}), .in3(ALU_outalu),
    .out({multiplexer_3_out_2, multiplexer_3_out}), .sel(muxB));  // open: in0
  Hex_Digit_Display hex_digit_display_15 (.value(multiplexer_1_out[3:0]));  // open: dp
  ALU_main ALU (
    .Cin(OutFlag[2]), .A(multiplexer_1_out), .B(main_1_outb), .FunSel(funsel_ALU), .OutAlu(ALU_outalu),
    .ZCNO(ALU_zcno));
  Hex_Digit_Display hex_digit_display_16 (.value(multiplexer_3_out));  // open: dp
  _2b_main Adress_Register_File (
    .FunSel(funsel_AR), .Input({multiplexer_3_out_2, multiplexer_3_out}), .OutC(Adress_Register_File_outc),
    .OutD(Adress_Register_File_outd), .OutDSel(outD_AR), .OutCSel(outC_AR), .RegSel(regsel_AR), .Clock(clk));
  Clock clock_1 (.out(clk));
  Hex_Digit_Display hex_digit_display_17 (.value(Adress_Register_File_outc[7:4]));  // open: dp
  Hex_Digit_Display hex_digit_display_18 (.value(Adress_Register_File_outd[3:0]));  // open: dp
  Hex_Digit_Display hex_digit_display_19 (.value(Adress_Register_File_outd[7:4]));  // open: dp
  Register #(.width(1)) register_1 (.D(ALU_zcno[0]), .en(1'b1), .Q(OutFlag[0]), .clk(clk), .clr(1'b0));
  Register #(.width(1)) register_2 (.D(ALU_zcno[1]), .en(1'b1), .Q(OutFlag[1]), .clk(clk), .clr(1'b0));
  Register #(.width(1)) register_3 (.D(ALU_zcno[2]), .en(1'b1), .Q(OutFlag[2]), .clk(clk), .clr(1'b0));
  Register #(.width(1)) register_4 (.D(ALU_zcno[3]), .en(1'b1), .Q(OutFlag[3]), .clk(clk), .clr(1'b0));
  Hex_Digit_Display hex_digit_display_20 (.value(Adress_Register_File_outc[3:0]));  // open: dp
  RAM #(.bus("separate")) ram_1 (
    .addr(Adress_Register_File_outd), .din(ALU_outalu), .data({ram_1_data_2, ram_1_data}), .str(1'b0),
    .clk(clk), .ld(read));  // open: sel, clr
  Hex_Digit_Display hex_digit_display_21 (.value(ram_1_data));  // open: dp
  Hex_Digit_Display hex_digit_display_22 (.value(ram_1_data_2));  // open: dp

  // Other names for the same wires on the sheet: Instruction[15:0] = {out_3, out_2}; Z = OutFlag[3]

  // Notes on the sheet:
  //   Register File
  //   Input
  //   OutA
  //   16-bit Regiter
  //   Input
  //   IR (0-7)
  //   OutB
  //   AR
  //   Input
  //   IR(8-15)
  //   A
  //   OutD
  //   OutC
  //   Memory Output
endmodule

module controller (
  input  clock,
  input  Z_Flag,
  input  [15:0] instruction,
  output [2:0] out_4,
  output enable,
  output [1:0] outd_ar,
  output l_h,
  output [1:0] \funsel_ır ,
  output read,
  output [2:0] regsel_ar,
  output [1:0] funsel_ar
);

  wire and_1_out, and_2_out, and_3_out, decoder_4_out0, decoder_4_out1, F1_1, F1_2, F1_3, F2_1,
       multiplexer_2_out, not_1_out, not_2_out, not_3_out, or_5_out, or_6_out, S1_AR, S1_PC, S1_R0, S1_R1,
       S1_R2, S1_R3, S1_SP, S2_AR, S2_PC, S2_R0, S2_R1, S2_R2, S2_R3, S2_SP, undriven;
  wire [0:0] or_1_out;
  wire [1:0] BR, CD;
  wire [2:0] F1, F2;
  wire [3:0] Destreg_R, Regsel;
  wire [7:0] AD, adder_1_out, multiplexer_1_out, register_1_q, register_2_q;

  and and_1 (and_1_out, BR[1], not_1_out, multiplexer_2_out);
  not not_1 (not_1_out, BR[0]);
  or or_1 (or_1_out[0], and_3_out, and_2_out);
  and and_2 (and_2_out, multiplexer_2_out, not_2_out);
  and and_3 (and_3_out, BR[1], BR[0]);
  Register register_1 (.D(adder_1_out), .en(and_1_out), .Q(register_1_q), .clk(clock));  // open: clr
  Multiplexer #(.select(2), .width(8), .enable("false")) multiplexer_1 (
    .in0(adder_1_out), .in1(AD), .in2(register_1_q), .in3({1'b1, instruction[15:11], 2'b00}),
    .out(multiplexer_1_out), .sel({BR[0], or_1_out[0]}));
  not not_2 (not_2_out, BR[0]);
  Multiplexer #(.select(2), .enable("false")) multiplexer_2 (
    .in0(1'b1), .in1(instruction[8]), .in2(Z_Flag), .in3(not_3_out), .out(multiplexer_2_out), .sel(CD));
  not not_3 (not_3_out, Z_Flag);
  or or_2 (read, F1_1, F1_2);
  Register register_2 (.D(multiplexer_1_out), .en(1'b1), .Q(register_2_q), .clk(clock));  // open: clr
  Adder adder_1 (.a(register_2_q), .b(8'h1), .out(adder_1_out));  // open: cin, cout
  ROM #(.dataWidth(18)) rom_1 (.addr(register_2_q), .data({F1, F2, CD, BR, AD}), .sel(undriven));
  Decoder #(.select(3), .enable("false")) decoder_1 (
    .out1(F1_1), .out2(F1_2), .out3(F1_3), .sel(F1));  // open: out0, out4, out5, out6, out7
  Decoder #(.select(3), .enable("false")) decoder_2 (
    .out1(F2_1), .sel(F2));  // open: out0, out2, out3, out4, out5, out6, out7
  assign funsel_ar = F2_1 ? 2'b10 : 2'bz;  // Controlled_Buffer controlled_buffer_1
  Decoder #(.select(2), .enable("false")) decoder_3 (
    .out0(Destreg_R[0]), .out1(Destreg_R[1]), .out2(Destreg_R[2]), .out3(Destreg_R[3]), .sel(instruction[9:8]));
  Decoder #(.select(2), .enable("false")) decoder_4 (
    .out0(decoder_4_out0), .out1(decoder_4_out1), .out2(out_4[1]), .out3(out_4[2]), .sel(instruction[9:8]));
  Decoder #(.select(2), .enable("false")) decoder_5 (
    .out0(Regsel[0]), .out1(Regsel[1]), .out2(Regsel[2]), .out3(Regsel[3]), .sel(instruction[10:9]));
  or or_3 (out_4[0], decoder_4_out0, decoder_4_out1);
  Decoder #(.select(3), .enable("false")) decoder_6 (
    .out0(S1_R0), .out1(S1_R1), .out2(S1_R2), .out3(S1_R3), .out4(S1_PC), .out5(S1_PC), .out6(S1_AR),
    .out7(S1_SP), .sel(instruction[7:5]));
  or or_4 (enable, F1_1, F1_2);
  assign regsel_ar = F2_1 ? 3'b001 : 3'bz;  // Controlled_Buffer controlled_buffer_2
  Decoder #(.select(3), .enable("false")) decoder_7 (
    .out0(S2_R0), .out1(S2_R1), .out2(S2_R2), .out3(S2_R3), .out4(S2_PC), .out5(S2_PC), .out6(S2_AR),
    .out7(S2_SP), .sel(instruction[4:2]));
  or or_5 (or_5_out, F1_1, F1_2);
  assign \funsel_ır  = or_5_out ? 2'b11 : 2'bz;  // Controlled_Buffer controlled_buffer_3
  assign l_h = F1_1 ? 1'b1 : 1'bz;  // Controlled_Buffer controlled_buffer_4
  assign l_h = F1_2 ? 1'b0 : 1'bz;  // Controlled_Buffer controlled_buffer_5
  or or_6 (or_6_out, F1_1, F1_2);
  assign outd_ar = or_6_out ? 2'b00 : 2'bz;  // Controlled_Buffer controlled_buffer_6

  // Other names for the same wires on the sheet: Adress[7:0] = instruction[7:0]; In0 = instruction[0];
  //   In1 = instruction[1]; In2 = instruction[2]; In3 = instruction[3]; In4 = instruction[4]; In5 = instruction[5];
  //   In6 = instruction[6]; In7 = instruction[7]; clk = clock; Destreg_AR[2:0] = out_4; funsel_IR[1:0] = \funsel_ır ;
  //   AdressMode = instruction[8]; In8 = instruction[8]; In9 = instruction[9]; In10 = instruction[10];
  //   In11 = instruction[11]; In12 = instruction[12]; In13 = instruction[13]; In14 = instruction[14];
  //   In15 = instruction[15]; Z = Z_Flag

  // Notes on the sheet:
  //   MAP
  //    INPUT LOGIC
  //   SBR
  //   Input
  //   Memory - read
  //   Incrementer
  //   Enable
  //   contents of rom_1 (hex, n*v repeats v):
  //   9001 11300 126*0 8081 18082 10083
  //   IR(15-8)<- M[PC]
  //   IR(7-0)<- M[PC]
  //   PC<- PC+1
  //   Microop
  //   Funsel- AR
  //   Regsel
  //   Destreg
  //   Instruction
  //   Adress mode
  //   0 im 1 dir
  //   Srcreg1
  //   Enable- IR
  //   Regsel- AR
  //   Adress
  //   Srcreg2
  //   Funsel - IR
  //   L/H - IR
  //   OutD- AR
endmodule
